# Fritzing sketch p2gstick (saved by Fritzing 0.8.3b)
breadboards: 1

parts:
  MT29F1G08ABADAWP_D1 = MT29F1G08ABADAWP:D [part_number=MT29F1G08ABADAWP:D package=tsop48]  # not connected
  IC1 = AT32UC3A3256S-ALUT [package=LQFP-144]  # not connected
  U1 = Voltage Regulator LM1117 [package=sot223]
  USBCONN = USB Connectors [package=usb-a-h]
  C3 = Ceramic Capacitor [capacitance=47µF package="0603 [SMD, multilayer]"]
  C4 = Ceramic Capacitor [capacitance=47µF package="0603 [SMD, multilayer]"]
  C5 = Ceramic Capacitor [capacitance=47µF package="0603 [SMD, multilayer]"]
  C6 = Ceramic Capacitor [capacitance=47µF package="0603 [SMD, multilayer]"]
  C7 = Ceramic Capacitor [capacitance=47µF package="0603 [SMD, multilayer]"]

nets:
  GND: U1.ADJ, USBCONN.GND, C3.1, C4.1, C5.1, C6.1, C7.1
  3.3V: U1.OUT, C3.0, C4.0, C5.0, C6.0, C7.0
  N1: U1.IN, USBCONN.D+

custom parts:
  MT29F1G08ABADAWP:D: Mircon MT29F1G08ABADAWP:D NAND flash
  AT32UC3A3256S-ALUT: IC1
